# Fritzing sketch smilemaskinenOpsætning (saved by Fritzing 0.9.3b)
breadboards: 1

parts:
  Part1 = Arduino Pro Mini (5V)
  R1 = Resistor [tolerance=±5% resistance=1k package=THT]
  R2 = Photocell (LDR) [package=THT]
  J1 = Basic Servo
  Q1 = Basic FET N-Channel [package="DPak [SMD]"]
  R3 = Resistor [tolerance=±5% resistance=10k package=THT]
  VCC1 = 4 x AAA Battery Mount

nets:
  N1: Part1.RAW, J1.vcc, VCC1.+
  N2: Part1.GND, R1.Pin_0, Q1.source, R3.Pin_1, VCC1.-
  N3: Part1.A0, R1.Pin_1, R2.pin_1
  N4: Part1.MISO, R2.pin_0
  N5: Part1.MOSI, J1.pulse
  N6: Part1.D10, Q1.Gate, R3.Pin_0
  N7: J1.gnd, Q1.drain
