# Fritzing sketch smilemaskinenPCB (saved by Fritzing 0.9.3b)
circuit board: 7.02915cm x 5.78779cm
breadboards: 1

parts:
  Pro_Mini = Arduino Pro Mini (5V)
  Q3 = MOSFET-NCHANNEL [package=to220v]
  J2 = Basic Servo
  R1 = Resistor [tolerance=±5% resistance=220 package="0603 [SMD]"]
  R2 = Photocell (LDR) [package=THT]
  R3 = Resistor [tolerance=±5% resistance=330 package="0603 [SMD]"]

nets:
  N1: Pro_Mini.GND, Q3.G, R1.Pin_1, R2.pin_0
  N2: Pro_Mini.A0, R2.pin_1, R3.Pin_0
  N3: Pro_Mini.MISO, R3.Pin_1
  N4: Pro_Mini.MOSI, J2.pulse
  N5: Pro_Mini.D10, Q3.S, R1.Pin_0
  N6: Q3.D, J2.gnd
